# Fritzing sketch prototype_sketch (saved by Fritzing 1.0.2b)
stripboards: 2

parts:
  U1 = LuaNode32 / ESP32 [part_number=ESP32S-PIN30]
  S1 = H-Bridge with L298N
  U2 = MAX6675 [package=so08]
  A1 = nozzle-bolt style thermocouple [package=THT]
  Part1 = LCD1602-I2C
  F1 = Fan - Ventilador [package=THT]
  RE1 = KY-040 Rotary encoder [package="Breakout board"]
  VCC1 = 4 x AAA Battery Mount
  BAT2 = Battery Holders [package=battery-aaa]
  BAT4 = Battery Holders [package=battery-aaa]
  BAT6 = Battery Holders [package=battery-aaa]
  BAT8 = Battery Holders [package=battery-aaa]
  BAT9 = Battery Holders [package=battery-aaa]
  BAT10 = Battery Holders [package=battery-aaa]
  BAT11 = Battery Holders [package=battery-aaa]
  BAT12 = Battery Holders [package=battery-aaa]
  BAT13 = Battery Holders [package=battery-aaa]
  BAT14 = Battery Holders [package=battery-aaa]

nets:
  N1: U1.D34, RE1.SW
  N2: U1.D35, RE1.DT
  N3: U1.D32, RE1.CLK
  N4: U1.D26, S1.IN2
  N5: U1.D27, S1.IN1
  N6: U1.D14, S1.ENA
  GND: U1.GND, S1.GND, U2.VSS, Part1.GND, RE1.GND, VCC1.-, BAT14.-
  VCC: U1.Vin, Part1.VCC, RE1.Vcc, VCC1.+
  3V3: U1.3V3, U2.VDD
  N7: U1.D2, Part1.SCL
  N8: U1.D4, Part1.SDA
  N9: U1.D5, U2.MISO
  N10: U1.D18, U2.CS
  N11: U1.D19, U2.SCK
  N12: S1.12V, BAT10.+
  N13: S1.M1-01, F1.5V
  N14: S1.M1-02, F1.GND
  N15: U2.T-, A1.pin2
  N16: U2.T+, A1.pin1
  N17: BAT2.-, BAT14.+
  N18: BAT2.+, BAT13.-
  N19: BAT4.-, BAT13.+
  N20: BAT4.+, BAT12.-
  N21: BAT6.-, BAT12.+
  N22: BAT6.+, BAT11.-
  N23: BAT8.-, BAT11.+
  N24: BAT8.+, BAT9.-
  N25: BAT9.+, BAT10.-

custom parts:
  LuaNode32 / ESP32: New Image for LuaNode32 DOIT ESP32 DEVKIT V1. Base parts from LuaNode32 / ESP32 ESP32 based LuaNode32 by G.Noorlander DOIT Esp32 DevKit v1 (30 pins long, 11 pins width) by Werner Rothschopf (modified by vanepp Dec 2018)
  H-Bridge with L298N: h-bridge
  nozzle-bolt style thermocouple: Generic nozzle-bolt style thermocouple.
  LCD1602-I2C: A standard character display, usually with 2x16 characters. Comes in many colors with LCM1602 IIC attached.
  Fan - Ventilador: Ventilador de 2 pines, se encuentra comunmente en computadoras de escritorio
  KY-040 Rotary encoder: KY-040 Rotary Encoder with switch on breakout borad from AZ Delivery
